# Fritzing sketch LDR_pulldown-register_ver2 (saved by Fritzing 0.9.0b)
breadboards: 1

parts:
  Part1 = Arduino Uno (Rev3)
  R2 = Resistor [tolerance=±5% resistance=1k package=THT]
  Part2 = Ambient Light Sensor (TEMT6000 Breakout Board)

nets:
  GND: Part1.GND, R2.Pin_0, Part2.GND
  N1: Part1.D3_PWM, R2.Pin_1, Part2.S
  5V: Part1.5V, Part2.VCC
